# Fritzing sketch Bot (saved by Fritzing 0.5.2b)
breadboards: 2

parts:
  Arduino1 = Arduino
  VCC2 = obsolete Battery
  M1 = DC Motor
  M2 = DC Motor
  R1 = Resistor [resistance=220 package=THT]
  R1_2 = Resistor [resistance=220 package=THT]
  Q2 = NPN-Transistor [package="TO92 [THT]"]
  Q1 = NPN-Transistor [package="TO92 [THT]"]
  S1 = Pushbutton [package=THT]
  S2 = Pushbutton [package=THT]
  R2 = Resistor [resistance=220 package=THT]
  R2_2 = Resistor [resistance=220 package=THT]
  R3 = Resistor [resistance=220 package=THT]
  R4 = Resistor [resistance=220 package=THT]

nets:
  N1: Arduino1.GND, VCC2.-, Q2.E, Q1.E, R2.Pin_1, R2_2.Pin_1
  N2: Arduino1.D10, R1_2.Pin_1
  N3: Arduino1.D9, R1.Pin_1
  N4: Arduino1.D3, R3.Pin_1
  N5: Arduino1.D2, R4.Pin_1
  N6: Arduino1.+5V, S1.leg0, S2.leg0
  N7: Arduino1.VIN, VCC2.+, M1.pin_1, M2.pin_1
  N8: M1.pin_2, Q1.C
  N9: M2.pin_2, Q2.C
  N10: R1.Pin_0, Q2.B
  N11: R1_2.Pin_0, Q1.B
  N12: S1.leg1, R2_2.Pin_0, R3.Pin_0
  N13: S2.leg1, R2.Pin_0, R4.Pin_0
