# Fritzing sketch Bot (saved by Fritzing 0.5.2b)
breadboards: 1

parts:
  Arduino1 = Arduino
  IC1 = H-Bridge [package=THT]
  M1 = DC Motor
  M2 = DC Motor
  J2 = Infrared Proximity Sensor
  J3 = Basic Servo
  S1 = Pushbutton [package=THT]
  S2 = Pushbutton [package=THT]

nets:
  GND: Arduino1.GND, IC1.GND1, IC1.GND2, IC1.GND3, IC1.GND4, J2.GND, J3.gnd, S1.leg0, S2.leg0
  N1: Arduino1.D13, IC1.4A
  N2: Arduino1.D12, IC1.3A
  N3: Arduino1.D11, IC1.3_4EN
  N4: Arduino1.D10, IC1.1_2EN
  N5: Arduino1.D8, IC1.2A
  N6: Arduino1.D7, IC1.1A
  N7: Arduino1.D5, S2.leg1
  N8: Arduino1.D4, S1.leg1
  N9: Arduino1.D3, J3.pulse
  N10: Arduino1.D2, J2.Vout
  VCC: Arduino1.+5V, IC1.VCC1, J2.Vcc, J3.vcc
  N11: Arduino1.VIN, IC1.VCC2
  N12: IC1.1Y, M1.pin_2
  N13: IC1.2Y, M1.pin_1
  N14: IC1.3Y, M2.pin_2
  N15: IC1.4Y, M2.pin_1

notes:
  VIN
  5v
